// Logisim project Circuit Project Logism.circ as structural Verilog: 1 circuit, main circuit main
// 6
module main (
);

  wire _1_q, _2_q, _3_q, _4_q, _5_q, _6_q, _7_q, ACK_out, and_1_out, and_2_out, and_3_out, and_4_out,
       and_5_out, and_6_out, and_7_out, and_8_out, and_9_out, and_10_out, and_11_out, and_12_out, and_13_out,
       and_14_out, and_15_out, and_16_out, and_17_out, and_18_out, clock_1_out, in_q, L1_out, L2_out, L3_out,
       L4_out, L5_out, L6_out, L7_out, not_1_out, not_2_out, or_1_out, or_2_out, or_3_out, or_4_out,
       or_5_out, or_6_out, or_7_out, or_8_out, or_9_out, Reset_out, TST_out;

  Button TST (.out(TST_out));
  Clock clock_1 (.out(clock_1_out));
  Button ACK (.out(ACK_out));
  Button Reset (.out(Reset_out));
  not not_1 (not_1_out, TST_out);
  not not_2 (not_2_out, ACK_out);
  and and_1 (and_1_out, TST_out, in_q);
  and and_2 (and_2_out, TST_out, _7_q);
  and and_3 (and_3_out, not_1_out, not_2_out, in_q);
  and and_4 (and_4_out, not_1_out, _7_q);
  and and_5 (and_5_out, ACK_out, not_1_out, in_q);
  and and_6 (and_6_out, not_2_out, not_1_out, _1_q);
  and and_7 (and_7_out, ACK_out, not_1_out, _6_q);
  and and_8 (and_8_out, ACK_out, not_1_out, _1_q);
  and and_9 (and_9_out, not_2_out, not_1_out, _2_q);
  and and_10 (and_10_out, ACK_out, not_1_out, _2_q);
  and and_11 (and_11_out, not_2_out, not_1_out, _3_q);
  and and_12 (and_12_out, ACK_out, not_1_out, _3_q);
  and and_13 (and_13_out, not_2_out, not_1_out, _4_q);
  and and_14 (and_14_out, ACK_out, not_1_out, _4_q);
  and and_15 (and_15_out, not_2_out, not_1_out, _5_q);
  and and_16 (and_16_out, ACK_out, not_1_out, _5_q);
  and and_17 (and_17_out, not_2_out, not_1_out, _6_q);
  or or_1 (or_1_out, and_5_out, and_6_out, and_7_out);
  or or_2 (or_2_out, and_16_out, and_17_out);
  or or_3 (or_3_out, and_1_out, and_2_out);
  or or_4 (or_4_out, and_3_out, and_18_out, and_4_out);
  or or_5 (or_5_out, and_8_out, and_9_out);
  or or_6 (or_6_out, and_10_out, and_11_out);
  or or_7 (or_7_out, and_12_out, and_13_out);
  or or_8 (or_8_out, and_14_out, and_15_out);
  D_Flip_Flop in (.clk(clock_1_out), .D(or_4_out), .Q(in_q), .preset(Reset_out));  // open: Qn, en, reset
  D_Flip_Flop _1 (.clk(clock_1_out), .D(or_1_out), .Q(_1_q), .reset(Reset_out));  // open: Qn, preset, en
  D_Flip_Flop _2 (.clk(clock_1_out), .D(or_5_out), .Q(_2_q), .reset(Reset_out));  // open: Qn, preset, en
  D_Flip_Flop _3 (.clk(clock_1_out), .D(or_6_out), .Q(_3_q), .reset(Reset_out));  // open: Qn, preset, en
  D_Flip_Flop _4 (.clk(clock_1_out), .D(or_7_out), .Q(_4_q), .reset(Reset_out));  // open: Qn, preset, en
  D_Flip_Flop _5 (.clk(clock_1_out), .D(or_8_out), .Q(_5_q), .reset(Reset_out));  // open: Qn, preset, en
  D_Flip_Flop _6 (.clk(clock_1_out), .D(or_2_out), .Q(_6_q), .reset(Reset_out));  // open: Qn, preset, en
  D_Flip_Flop _7 (.clk(clock_1_out), .D(or_3_out), .Q(_7_q), .reset(Reset_out));  // open: Qn, preset, en
  or or_9 (or_9_out, _1_q, _2_q, _3_q, _4_q, _5_q, _6_q);
  and and_18 (and_18_out, or_9_out, TST_out);
  or L4 (L4_out, _1_q, _3_q, _5_q, _7_q);
  or L1 (L1_out, _2_q, _3_q, _4_q, _5_q, _6_q, _7_q);
  or L6 (L6_out, _6_q, _7_q);
  or L2 (L2_out, _6_q, _7_q);
  or L3 (L3_out, _4_q, _5_q, _6_q, _7_q);
  or L5 (L5_out, _6_q, _7_q, _5_q, _4_q);
  or L7 (L7_out, _2_q, _3_q, _4_q, _5_q, _6_q, _7_q);
  LED led_1 (.in(L1_out));
  LED led_2 (.in(L4_out));
  LED led_3 (.in(L2_out));
  LED led_4 (.in(L3_out));
  LED led_5 (.in(L5_out));
  LED led_6 (.in(L6_out));
  LED led_7 (.in(L7_out));
endmodule
